# Fritzing sketch HamlalC25Module_I2C_control_LED_V01 (saved by Fritzing 0.8.5b)
breadboards: 1

parts:
  LED6M = LED - 5mm [color="Red (633nm)" package="5 mm [THT]"]
  Arduino_UNO = Arduino Uno (Rev3)
  R1 = Resistor [tolerance=±5% resistance=220 package=THT]
  BAND = Rotary Encoder [package=THT]
  PTT = Pushbutton [package="[THT]"]
  LED10M = LED - 5mm [color="Red (633nm)" package="5 mm [THT]"]
  LED20M = LED - 5mm [color="Red (633nm)" package="5 mm [THT]"]
  LED15M = LED - 5mm [color="Red (633nm)" package="5 mm [THT]"]
  R3 = Resistor [tolerance=±5% resistance=220 package=THT]
  R4 = Resistor [tolerance=±5% resistance=220 package=THT]
  LED80M = LED - 5mm [color="Red (633nm)" package="5 mm [THT]"]
  LED160M = LED - 5mm [color="Red (633nm)" package="5 mm [THT]"]
  LEDPTT = LED - 5mm [color="Red (633nm)" package="5 mm [THT]"]
  LED40M = LED - 5mm [color="Red (633nm)" package="5 mm [THT]"]
  R5 = Resistor [tolerance=±5% resistance=220 package=THT]
  R6 = Resistor [tolerance=±5% resistance=220 package=THT]
  R7 = Resistor [tolerance=±5% resistance=220 package=THT]
  R8 = Resistor [tolerance=±5% resistance=220 package=THT]
  R2 = Resistor [tolerance=±5% resistance=220 package=THT]
  R9 = Resistor [tolerance=±5% resistance=220 package=THT]

nets:
  N1: LED6M.cathode, R1.Pin_1
  N2: LED6M.anode, Arduino_UNO.D13/SCK
  N3: Arduino_UNO.D8, LED160M.anode
  N4: Arduino_UNO.D9_PWM, BAND.EncoderPinC
  N5: Arduino_UNO.D10_PWM/SS, BAND.EncoderPinA
  N6: Arduino_UNO.D11_PWM/MOSI, Arduino_UNO.VIN, PTT.Pin_1, PTT.Pin_2, PTT.Pin_3, PTT.Pin_4, R9.Pin_0, R9.Pin_1
  N7: Arduino_UNO.D3_PWM, LED10M.anode
  N8: Arduino_UNO.D4, LED15M.anode
  N9: Arduino_UNO.D5_PWM, LED20M.anode
  N10: Arduino_UNO.D6_PWM, LED40M.anode
  N11: Arduino_UNO.D7, LED80M.anode
  N12: Arduino_UNO.GND, R1.Pin_0, BAND.EncoderPinB, R3.Pin_0, R4.Pin_0, R5.Pin_0, R6.Pin_0, R7.Pin_0, R8.Pin_0, R2.Pin_0
  N13: LED10M.cathode, R2.Pin_1
  N14: LED20M.cathode, R4.Pin_1
  N15: LED15M.cathode, R3.Pin_1
  N16: LED80M.cathode, R7.Pin_1
  N17: LED160M.cathode, R5.Pin_1
  N18: LEDPTT.cathode, R8.Pin_1
  N19: LED40M.cathode, R6.Pin_1
